// Logisim project Carry_LookAheadAdder.circ as structural Verilog: 1 circuit, main circuit main
module main (
  input  X,
  input  Y,
  input  C1
);

  wire and_1_out, and_2_out, xor_1_out;

  xor xor_1 (xor_1_out, X, Y);
  and and_1 (and_1_out, Y, X);
  // XOR_Gate xor_2 has open pins: in0=xor_1_out, in1=C1, out=open
  and and_2 (and_2_out, xor_1_out, C1);
  // OR_Gate or_1 has open pins: in0=and_2_out, in1=and_1_out, out=open

  // Notes on the sheet:
  //   Carry LookAhead Adder
endmodule
