// Logisim project Full_Adder.circ as structural Verilog: 1 circuit, main circuit main
module main (
  input  x,
  input  y,
  input  Carry_In,
  output S,
  output C
);

  wire and_1_out, and_2_out, xor_1_out;

  and and_1 (and_1_out, x, y);
  xor xor_1 (xor_1_out, x, y);
  xor xor_2 (S, xor_1_out, Carry_In);
  and and_2 (and_2_out, xor_1_out, Carry_In);
  or or_1 (C, and_2_out, and_1_out);

  // Notes on the sheet:
  //   FULL ADDER
endmodule
