// Logisim project Ripple_Carry_Adder.circ as structural Verilog: 1 circuit, main circuit main
module main (
  input  X1,
  input  X0,
  input  Y1,
  input  Y0,
  input  Carry_In,
  input  Input_Xn,
  input  Input_Yn,
  output S1,
  output S0,
  output C,
  output Sum_N,
  output Carry_out
);

  wire and_1_out, and_2_out, and_3_out, and_4_out, and_5_out, and_6_out, or_1_out, undriven, xor_1_out,
       xor_3_out, xor_5_out;

  and and_1 (and_1_out, X0, Y0);
  xor xor_1 (xor_1_out, X0, Y0);
  xor xor_2 (S0, xor_1_out, Carry_In);
  and and_2 (and_2_out, xor_1_out, Carry_In);
  and and_3 (and_3_out, Input_Xn, Input_Yn);
  or or_1 (or_1_out, and_2_out, and_1_out);
  xor xor_3 (xor_3_out, Input_Xn, Input_Yn);
  xor xor_4 (Sum_N, xor_3_out, undriven);
  and and_4 (and_4_out, xor_3_out, undriven);
  or or_2 (Carry_out, and_4_out, and_3_out);
  xor xor_5 (xor_5_out, X1, Y1);
  and and_5 (and_5_out, X1, Y1);
  xor xor_6 (S1, xor_5_out, or_1_out);
  and and_6 (and_6_out, xor_5_out, or_1_out);
  or or_3 (C, and_6_out, and_5_out);

  // Notes on the sheet:
  //   Input for carry out
  //   Keep in mind that Sum0 is the LSB and Sum1 is MSB. The Smallest SumN is the LSB and the largest SumN is the MSB
  //   You can increase the amount of bits by copying the full adder, and placing it in the sequence of Ripple Carry Adders.
  //   Two Bit Ripple Carry Adder
  //   Carry out is passed as Carry in.
endmodule
