// Logisim project Decoder.circ as structural Verilog: 1 circuit, main circuit main
module main (
  input  X,
  input  Y,
  input  Z,
  output Zero,
  output One,
  output Two,
  output Three,
  output Four,
  output Five,
  output Six,
  output Seven
);

  and D0 (Zero, ~X, ~Y, ~Z);  // AND_Gate
  and D1 (One, ~X, ~Y, Z);  // AND_Gate
  and D2 (Two, ~X, Y, ~Z);  // AND_Gate
  and D3 (Three, ~X, Y, Z);  // AND_Gate
  and D4 (Four, X, ~Y, ~Z);  // AND_Gate
  and D5 (Five, X, ~Y, Z);  // AND_Gate
  and D6 (Six, X, Y, ~Z);  // AND_Gate
  and D7 (Seven, X, Y, Z);

  // Notes on the sheet:
  //   Decoder
endmodule
