// Logisim project 4x2_Encoder.circ as structural Verilog: 1 circuit, main circuit main
module main (
  input  Zero,
  input  One,
  input  Two,
  input  Three,
  output LSB,
  output MSB
);

  or or_1 (LSB, One, Three);
  or or_2 (MSB, Two, Three);

  // Notes on the sheet:
  //   4x2 Encoder
endmodule
