// Logisim project 8x3_Encoder.circ as structural Verilog: 1 circuit, main circuit main
module main (
  input  Zero,
  input  One,
  input  Two,
  input  Three,
  input  Four,
  input  Five,
  input  Six,
  input  Seven,
  output out_9,
  output out_10,
  output out_11
);

  or LSB (out_9, One, Five, Seven, Three);
  or or_1 (out_10, Two, Six, Seven, Three);
  or MSB (out_11, Four, Six, Seven, Five);

  // Notes on the sheet:
  //   (Does not connect to anything)
  //   ENCODER
  //   Three Bit Encoder (8x3)
endmodule
