// Logisim project Half_Adder.circ as structural Verilog: 1 circuit, main circuit main
module main (
  input  x,
  input  y,
  output Sum,
  output Carry
);

  xor xor_1 (Sum, x, y);
  and and_1 (Carry, x, y);

  // Notes on the sheet:
  //   HALF ADDER
endmodule
