// Logisim project 1_Bit_multiplexer.circ as structural Verilog: 1 circuit, main circuit main
module main (
  input  I0,
  input  I1,
  input  S,
  output Y
);

  wire and_1_out, and_2_out;

  and and_1 (and_1_out, I0, ~S);  // AND_Gate
  and and_2 (and_2_out, I1, S);
  or or_1 (Y, and_1_out, and_2_out);

  // Notes on the sheet:
  //   1 Bit Multiplexer
endmodule
