// Logisim project Actual_2BitMulti.circ as structural Verilog: 1 circuit, main circuit main
module main (
  input  I0,
  input  I1,
  input  I2,
  input  I3,
  input  S0,
  input  S1,
  output out_7
);

  wire IN0_out, IN1_out, IN2_out, IN3_out;

  and IN0 (IN0_out, I0, ~S0, ~S1);  // AND_Gate
  and IN1 (IN1_out, I1, ~S0, S1);  // AND_Gate
  and IN2 (IN2_out, I2, S0, ~S1);  // AND_Gate
  and IN3 (IN3_out, I3, S0, S1);
  or or_1 (out_7, IN0_out, IN1_out, IN2_out, IN3_out);

  // Notes on the sheet:
  //   2 Bit Multiplexer
endmodule
