// Logisim project Subtractor_Circuit.circ as structural Verilog: 1 circuit, main circuit main
module main (
  input  Mode,
  input  B0,
  input  A0,
  input  B1,
  input  A1,
  input  B2,
  input  A2,
  output S0,
  output S1,
  output S2,
  output OverFlow,
  output Carry
);

  wire adder_1_cout, adder_2_cout, xor_1_out, xor_2_out, xor_3_out;

  xor xor_1 (xor_1_out, Mode, B0);
  xor xor_2 (xor_2_out, Mode, B1);
  xor xor_3 (xor_3_out, Mode, B2);
  Adder #(.width(1)) adder_1 (.a(xor_1_out), .b(A0), .out(S0), .cin(Mode), .cout(adder_1_cout));
  Adder #(.width(1)) adder_2 (.a(xor_2_out), .b(A1), .out(S1), .cin(adder_1_cout), .cout(adder_2_cout));
  Adder #(.width(1)) adder_3 (.a(xor_3_out), .b(A2), .out(S2), .cin(adder_2_cout), .cout(Carry));
  xor xor_4 (OverFlow, adder_2_cout, Carry);

  // Notes on the sheet:
  //   Subtractor
endmodule
